# Fritzing sketch Modélisation Fridge Fit (saved by Fritzing 0.9.3b)
breadboards: 1

parts:
  Composant1 = Arduino Uno (Rev3)
  DHT1 = DHT22 Humidity and Temperature Sensor
  J1 = Peltier Element
  R1 = Temperature Sensor (Thermistor) [thermistor_type=NTC package=THT]
  BAT1 = BC9VPC [package=bc9vpc]
  Q1 = Basic FET N-Channel [package="DPak [SMD]"]
  R2 = Resistor [tolerance=±5% resistance=10k package="0603 [SMD]"]
  R4 = Resistor [tolerance=±5% resistance=10k package="0603 [SMD]"]
  R5 = Temperature Sensor (Thermistor) [thermistor_type=NTC package=THT]
  R6 = Resistor [tolerance=±5% resistance=10k package="0603 [SMD]"]
  R3 = Resistor [tolerance=±5% resistance=5.6k package="0805 [SMD]"]

nets:
  N1: Composant1.A0, R1.pin_1, R3.Pin_0
  N2: Composant1.A1, R5.pin_1, R6.Pin_0
  GND: Composant1.GND, DHT1.GND, R1.pin_0, BAT1.V-, Q1.source, R4.Pin_0, R5.pin_0
  N3: Composant1.D2, DHT1.DATA, R2.Pin_1
  N4: Composant1.D6_PWM, Q1.Gate, R4.Pin_1
  5V: Composant1.5V, DHT1.VDD, R2.Pin_0, R6.Pin_1, R3.Pin_1
  N5: J1.pin1, Q1.drain
  N6: J1.pin2, BAT1.V+
